# Fritzing sketch Automatic Street Light Using Arduino Circuit Diagram (saved by Fritzing 0.9.3b)
breadboards: 1

parts:
  R1 = Photocell (LDR) [package=THT]
  Mod1 = KY-019 5V Relay Module [package="Breakout board"]
  Part1 = Arduino Uno (Rev3)
  R2 = Resistor [tolerance=±5% resistance=220 package=THT]
  J2 = Screw terminal - 2 pins [package=THT]
  LED1 = LEDs [package=led10mm]

nets:
  N1: R1.pin_0, Mod1.+, Part1.5V
  N2: R1.pin_1, Part1.A0, R2.Pin_0
  N3: Mod1.S, Part1.D5_PWM
  N4: Mod1.-, Part1.GND, R2.Pin_1
  N5: Mod1.Common, J2.pin2
  N6: Mod1.NO, LED1.C
  N7: J2.pin1, LED1.A

notes:
  AC Supply
  AC Bulb
  Arduino Uno
  LDR Sensor
  10 Resistance
  Relay Module

custom parts:
  KY-019 5V Relay Module: KY-019 5V Relay module, used to control AC circuits. (Special thanks to vanepp for fixing the PCB holes and other errors)
