# Fritzing sketch Hand Gesture Conttrol Wheel Chair Model (saved by Fritzing 0.9.3b)
breadboards: 1

parts:
  L298N3 = L298N DC motor driver
  M3 = DC Motor
  M4 = DC Motor
  BAT3 = BC9VPC [package=bc9vpc]
  Part2 = Arduino Uno (Rev3) - ICSP
  Part3 = Triple Axis Accelerometer Breakout - ADXL345

nets:
  N1: L298N3.OUT1, M3.pin_2
  N2: L298N3.OUT2, M3.pin_1
  N3: L298N3.OUT3, M4.pin_2
  N4: L298N3.OUT4, M4.pin_1
  N5: L298N3.12V, BAT3.V+
  GND: L298N3.GND, BAT3.V-, Part2.GND, Part3.GND
  5V: L298N3.5V, Part2.5V, Part3.VCC
  N6: L298N3.IN1, Part2.D13/SCK
  N7: L298N3.IN2, Part2.D12/MISO
  N8: L298N3.IN3, Part2.D11_PWM/MOSI
  N9: L298N3.IN4, Part2.D10_PWM/SS
  N10: Part2.A4/SDA, Part3.SDA
  N11: Part2.A5/SCL, Part3.SCL

notes:
  Hand Gesture Control Wheel Chair Model
  S S Kale

custom parts:
  L298N DC motor driver: 2x DC motor driver with 78M05 positive voltage regulator (7..35 V) L298N: max 46 V, 2 A Set 5 V Enable jumper to enable 5 V regultor (needed for the L298N) and +5 V output at screw terminal or supply external +5 V at screw terminal Set ENA and/or ENB to +5 V to enable motor permanently or supply ENA and/or ENB with PWM signal IN1 and IN2 set rotation directory for motor A (OUT1/OUT2) IN2 and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
