# Fritzing sketch IOT Based Pick and Place (saved by Fritzing 0.9.3b)
breadboards: 1

parts:
  U3 = ESP32-38PinWide [part_number=ESP32-38PinWide]
  L298N2 = L298N DC motor driver
  BAT2 = BC9VPC [package=bc9vpc]
  J1 = Basic Servo
  J2 = Basic Servo
  M1 = DC Motor
  M2 = DC Motor

nets:
  N1: U3.GPIO33, J1.pulse
  VCC: U3.GPIO25, U3.VIN, L298N2.5V, J1.vcc, J2.vcc, J2.pulse
  N2: U3.GPIO26, L298N2.IN1
  N3: U3.GPIO27, L298N2.IN2
  N4: U3.GPIO14, L298N2.IN3
  N5: U3.GPIO12, L298N2.IN4
  GND: U3.GND, L298N2.GND, BAT2.V-, J1.gnd, J2.gnd
  N6: L298N2.OUT1, M2.pin_2
  N7: L298N2.OUT2, M2.pin_1
  N8: L298N2.OUT3, M1.pin_2
  N9: L298N2.OUT4, M1.pin_1
  N10: L298N2.12V, BAT2.V+

notes:
  Web Controlling Pick and Place Robot
  S S Kale

custom parts:
  ESP32-38PinWide: Generic 38-Pin ESP32 with wide format (only access to one side of pins on a breadboard) based on Stephen Lilley's HiLetgo ESP-WROOM-32 ESP32 ESP-32S Development Board.
  L298N DC motor driver: 2x DC motor driver with 78M05 positive voltage regulator (7..35 V) L298N: max 46 V, 2 A Set 5 V Enable jumper to enable 5 V regultor (needed for the L298N) and +5 V output at screw terminal or supply external +5 V at screw terminal Set ENA and/or ENB to +5 V to enable motor permanently or supply ENA and/or ENB with PWM signal IN1 and IN2 set rotation directory for motor A (OUT1/OUT2) IN2 and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
