# Fritzing sketch IOT Car Parking usinf ESp32 (saved by Fritzing 0.9.3b)
circuit board: 20.0308cm x 12.4857cm
breadboards: 1

parts:
  M1 = fc-51 [package=THT]
  M2 = fc-51 [package=THT]
  M3 = fc-51 [package=THT]
  M4 = fc-51 [package=THT]
  M5 = fc-51 [package=THT]
  M6 = fc-51 [package=THT]
  M7 = fc-51 [package=THT]
  M8 = fc-51 [package=THT]
  U1 = ESP32-38PinWide [part_number=ESP32-38PinWide]
  J1 = Basic Servo
  J2 = Basic Servo
  BAT1 = BC9VPC [package=bc9vpc]
  VCC1 = Battery
  J3 = Screw terminal - 2 pins [package=THT]

nets:
  N1: M1.pin1, U1.GPIO12
  GND: M1.pin2, M2.pin2, M3.pin2, M4.pin2, M5.pin2, M6.pin2, M7.pin2, M8.pin2, U1.GND, J2.gnd, BAT1.V-, VCC1.-, J3.pin2
  VCC: M1.pin3, M2.pin3, M3.pin3, M4.pin3, M5.pin3, M6.pin3, M7.pin3, M8.pin3, J1.vcc, J2.vcc, BAT1.V+, J3.pin1
  N2: M2.pin1, U1.GPIO14
  N3: M3.pin1, U1.GPIO27
  N4: M4.pin1, U1.GPIO25
  N5: M5.pin1, U1.GPIO26
  N6: M6.pin1, U1.GPIO33
  N7: M7.pin1, U1.GPIO32
  N8: M8.pin1, U1.GPIO35
  N9: U1.VIN, VCC1.+
  N10: U1.GPIO15, J1.pulse
  N11: U1.GPIO2, J2.pulse

notes:
  IOT Car Parking using ESP32
  S S Kale
  ESP32
  Servo Motor
  Battries
  IR Sensor

custom parts:
  ESP32-38PinWide: Generic 38-Pin ESP32 with wide format (only access to one side of pins on a breadboard) based on Stephen Lilley's HiLetgo ESP-WROOM-32 ESP32 ESP-32S Development Board.
