# Fritzing sketch IOT Car parking (saved by Fritzing 0.9.3b)
breadboards: 1

parts:
  M1 = fc-51 [package=THT]
  M2 = fc-51 [package=THT]
  M3 = fc-51 [package=THT]
  M4 = fc-51 [package=THT]
  M5 = fc-51 [package=THT]
  M6 = fc-51 [package=THT]
  M7 = fc-51 [package=THT]
  M8 = fc-51 [package=THT]
  U1 = ESP32-38PinWide [part_number=ESP32-38PinWide]
  J1 = Basic Servo
  J2 = Basic Servo
  BAT1 = BC9VPC [package=bc9vpc]
  VCC1 = Battery

nets:
  GND: M1.pin2, M2.pin2, M3.pin2, M4.pin2, M5.pin2, M6.pin2, M7.pin2, M8.pin2, U1.GND, J2.gnd, BAT1.V-, VCC1.-
  VCC: M1.pin3, M2.pin3, M3.pin3, M4.pin3, M5.pin3, M6.pin3, M7.pin3, M8.pin3, J1.vcc, J2.vcc, BAT1.V+
  N1: U1.VIN, VCC1.+
  N2: U1.GPIO15, J1.pulse
  N3: U1.GPIO2, J2.pulse

notes:
  IOT Car Parking using ESP32
  S S Kale

custom parts:
  ESP32-38PinWide: Generic 38-Pin ESP32 with wide format (only access to one side of pins on a breadboard) based on Stephen Lilley's HiLetgo ESP-WROOM-32 ESP32 ESP-32S Development Board.
