# Fritzing sketch IOT based wheel chair (saved by Fritzing 0.9.3b)
breadboards: 1

parts:
  U1 = ESP32-38PinWide [part_number=ESP32-38PinWide]
  L298N1 = L298N DC motor driver
  BAT1 = BC9VPC [package=bc9vpc]
  U2 = MLX90614 [package=to-39]
  IC1 = Voltage Regulator [package=78xxl]
  C1 = Electrolytic Capacitor [capacitance=1000µF package="300 mil [THT, electrolytic]"]
  C2 = Electrolytic Capacitor [capacitance=1000µF package="300 mil [THT, electrolytic]"]

nets:
  N1: U1.GPIO26, L298N1.IN1
  N2: U1.GPIO27, L298N1.IN2
  N3: U1.GPIO14, L298N1.IN3
  N4: U1.GPIO12, L298N1.IN4
  GND: U1.GND, L298N1.GND, BAT1.V-, U2.VSS, C2.-
  VIN: U1.VIN, L298N1.5V
  N5: U1.GPIO21, U2.PWM_SDA
  N6: U1.GPIO22, U2.SCL_VZ
  N7: BAT1.V+, IC1.IN, C1.+
  N8: U2.VDD, IC1.OUT, C2.+
  N9: IC1.GND, C1.-

custom parts:
  ESP32-38PinWide: Generic 38-Pin ESP32 with wide format (only access to one side of pins on a breadboard) based on Stephen Lilley's HiLetgo ESP-WROOM-32 ESP32 ESP-32S Development Board.
  L298N DC motor driver: 2x DC motor driver with 78M05 positive voltage regulator (7..35 V) L298N: max 46 V, 2 A Set 5 V Enable jumper to enable 5 V regultor (needed for the L298N) and +5 V output at screw terminal or supply external +5 V at screw terminal Set ENA and/or ENB to +5 V to enable motor permanently or supply ENA and/or ENB with PWM signal IN1 and IN2 set rotation directory for motor A (OUT1/OUT2) IN2 and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
