# Fritzing sketch IR Remote Control  Appliances Circuit Diagram Fritzing (saved by Fritzing 0.9.3b)
breadboards: 1

parts:
  Mod1 = KY-019 5V Relay Module [package="Breakout board"]
  Part1 = Arduino Uno (Rev3)
  IR2 = tl1838_1
  LED1 = LEDs [package=led10mm]
  J1 = Screw terminal - 2 pins [package=THT]

nets:
  N1: Mod1.S, Part1.D3_PWM
  N2: Mod1.+, Part1.5V, IR2.connector2
  N3: Mod1.-, Part1.GND, IR2.connector1
  N4: Mod1.Common, J1.pin2
  N5: Mod1.NO, LED1.A
  N6: Part1.D2, IR2.connector0
  N7: LED1.C, J1.pin1

notes:
  250V Ac Supply
  Relay Module
  Arduino Uno
  TSOP 1838

custom parts:
  KY-019 5V Relay Module: KY-019 5V Relay module, used to control AC circuits. (Special thanks to vanepp for fixing the PCB holes and other errors)
  LEDs: LEDs Standard schematic elements and footprints for 5mm, 3mm, 1206, and 0603 sized LEDs. 5mm - Spark Fun Electronics SKU : COM-00529 (and others)
