# Fritzing sketch Smart Car Parking Using IOT (saved by Fritzing 0.9.3b)
circuit board: 20.0308cm x 12.4857cm
breadboards: 1

parts:
  M1 = fc-51 [package=THT]
  M2 = fc-51 [package=THT]
  M3 = fc-51 [package=THT]
  M4 = fc-51 [package=THT]
  M5 = fc-51 [package=THT]
  M6 = fc-51 [package=THT]
  M7 = fc-51 [package=THT]
  M8 = fc-51 [package=THT]
  U1 = ESP32-38PinWide [part_number=ESP32-38PinWide]
  J1 = Basic Servo
  J3 = Screw terminal - 2 pins [package=THT]
  C1 = Capacitor Polarized [package=cpol-radial-1000uf-63v]
  C2 = Capacitor Polarized [package=cpol-radial-1000uf-63v]
  U2 = Voltage Regulator - 5V [package="TO220 [THT]"]
  D1 = bridge rectifier round [package="round [THT]"]
  U3 = Transformer [package=transformer]

nets:
  N1: M1.pin1, U1.GPIO12
  GND: M1.pin2, M2.pin2, M3.pin2, M4.pin2, M5.pin2, M6.pin2, M7.pin2, M8.pin2, U1.GND, J1.gnd, J3.pin2, C1.-, C2.-, U2.GND, D1.DC-
  VIN: M1.pin3, M2.pin3, M3.pin3, M4.pin3, M5.pin3, M6.pin3, M7.pin3, M8.pin3, U1.VIN, J1.vcc, J3.pin1, C2.+, U2.output_voltage
  N2: M2.pin1, U1.GPIO14
  N3: M3.pin1, U1.GPIO27
  N4: M4.pin1, U1.GPIO25
  N5: M5.pin1, U1.GPIO26
  N6: M6.pin1, U1.GPIO33
  N7: M7.pin1, U1.GPIO32
  N8: M8.pin1, U1.GPIO35
  N9: U1.GPIO15, J1.pulse
  N10: C1.+, U2.input_voltage, D1.DC+
  N11: D1.AC#0, U3.5
  N12: D1.AC#1, U3.3

notes:
  Smart Car Parking Using IOT
  ESP32
  Servo Motor
  Power Suply
  IR Sensor for Slots
  IR Sensor for Gate
  S S Kale

custom parts:
  ESP32-38PinWide: Generic 38-Pin ESP32 with wide format (only access to one side of pins on a breadboard) based on Stephen Lilley's HiLetgo ESP-WROOM-32 ESP32 ESP-32S Development Board.
  Transformer: Small transformers
